// Logisim project nincpu.circ as structural Verilog
module HalfAdder (
  input  Cin,
  input  Ax,
  input  Bx,
  output Res,
  output Cout
);

  wire and_1_out, and_2_out, and_3_out, and_4_out, xor_1_out;

  and and_1 (and_1_out, Ax, Cin);
  and and_2 (and_2_out, Ax, Bx);
  or or_1 (Cout, and_1_out, and_2_out, and_3_out);
  and and_3 (and_3_out, Bx, Cin);
  ExactlyOne xor_1 (.out(xor_1_out), .in0(Ax), .in1(Bx), .in2(Cin));
  and and_4 (and_4_out, Ax, Bx, Cin);
  or or_2 (Res, xor_1_out, and_4_out);
endmodule

module FullAdder (
  input  Cin,
  input  [7:0] B,
  input  [7:0] A,
  output [7:0] C,
  output Cout
);

  wire halfadder_1_cout, halfadder_2_cout, halfadder_3_cout, halfadder_4_cout, halfadder_5_cout,
       halfadder_6_cout, halfadder_7_cout;

  HalfAdder halfadder_1 (.Cin(Cin), .Ax(A[0]), .Bx(B[0]), .Res(C[0]), .Cout(halfadder_1_cout));
  HalfAdder halfadder_2 (.Cin(halfadder_1_cout), .Ax(A[1]), .Bx(B[1]), .Res(C[1]), .Cout(halfadder_2_cout));
  HalfAdder halfadder_3 (.Cin(halfadder_2_cout), .Ax(A[2]), .Bx(B[2]), .Res(C[2]), .Cout(halfadder_3_cout));
  HalfAdder halfadder_4 (.Cin(halfadder_3_cout), .Ax(A[3]), .Bx(B[3]), .Res(C[3]), .Cout(halfadder_4_cout));
  HalfAdder halfadder_5 (.Cin(halfadder_4_cout), .Ax(A[4]), .Bx(B[4]), .Res(C[4]), .Cout(halfadder_5_cout));
  HalfAdder halfadder_6 (.Cin(halfadder_5_cout), .Ax(A[5]), .Bx(B[5]), .Res(C[5]), .Cout(halfadder_6_cout));
  HalfAdder halfadder_7 (.Cin(halfadder_6_cout), .Ax(A[6]), .Bx(B[6]), .Res(C[6]), .Cout(halfadder_7_cout));
  HalfAdder halfadder_8 (.Cin(halfadder_7_cout), .Ax(A[7]), .Bx(B[7]), .Res(C[7]), .Cout(Cout));
endmodule

module FullAdderSubstracter (
  input  Sr,
  input  [7:0] B,
  input  [7:0] A,
  output [7:0] C
);

  wire [7:0] not_1_out;

  assign not_1_out = ~B;  // NOT_Gate not_1, 8 bits wide
  FullAdder fulladder_1 (.Cin(1'b1), .B(not_1_out), .A(A), .C(C));  // open: Cout

  // Notes on the sheet:
  //   Sr = 1 -> sum
endmodule
