// Logisim project nincpu_alu.circ as structural Verilog: 4 circuits, main circuit ALU
module ALU (
  input  Op,
  input  [15:0] A,
  input  [15:0] B,
  output Z,
  output O,
  output N,
  output C,
  output [15:0] Res
);

  wire or_1_out;

  sixteenAdderSubstracter sixteenaddersubstracter_1 (.As(Op), .B(B), .A(A), .Res({N, Res[14:0]}), .Carry(C));
  xor xor_1 (O, C, Op);
  or or_1 (or_1_out, Res[0], Res[1], Res[2], Res[3], Res[4], Res[5], Res[6], Res[7], Res[8], Res[9], Res[10], Res[11], Res[12], Res[13], Res[14], N);
  not not_1 (Z, or_1_out);

  assign Res[15] = N;
endmodule

module sixteenAdderSubstracter (
  input  As,
  input  [15:0] B,
  input  [15:0] A,
  output [15:0] Res,
  output Carry
);

  wire [15:0] xor_16_out;

  xor xor_1 (xor_16_out[15], As, B[15]);
  xor xor_2 (xor_16_out[14], As, B[14]);
  xor xor_3 (xor_16_out[13], As, B[13]);
  xor xor_4 (xor_16_out[12], As, B[12]);
  xor xor_5 (xor_16_out[11], As, B[11]);
  xor xor_6 (xor_16_out[10], As, B[10]);
  xor xor_7 (xor_16_out[9], As, B[9]);
  xor xor_8 (xor_16_out[8], As, B[8]);
  xor xor_9 (xor_16_out[7], As, B[7]);
  xor xor_10 (xor_16_out[6], As, B[6]);
  xor xor_11 (xor_16_out[5], As, B[5]);
  xor xor_12 (xor_16_out[4], As, B[4]);
  xor xor_13 (xor_16_out[3], As, B[3]);
  xor xor_14 (xor_16_out[2], As, B[2]);
  xor xor_15 (xor_16_out[1], As, B[1]);
  xor xor_16 (xor_16_out[0], As, B[0]);
  sixteenAdder sixteenadder_1 (.Cin(As), .B(xor_16_out), .A(A), .C(Res), .Cout(Carry));

  // Notes on the sheet:
  //   As = 0 -> sum
endmodule

module sixteenAdder (
  input  Cin,
  input  [15:0] B,
  input  [15:0] A,
  output [15:0] C,
  output Cout
);

  wire fulladder_1_cout, fulladder_2_cout, fulladder_3_cout, fulladder_4_cout, fulladder_5_cout,
       fulladder_6_cout, fulladder_7_cout, fulladder_8_cout, fulladder_9_cout, fulladder_10_cout,
       fulladder_11_cout, fulladder_12_cout, fulladder_13_cout, fulladder_14_cout, fulladder_15_cout;

  fullAdder fulladder_1 (.Cin(Cin), .Ax(A[0]), .Bx(B[0]), .Res(C[0]), .Cout(fulladder_1_cout));
  fullAdder fulladder_2 (.Cin(fulladder_1_cout), .Ax(A[1]), .Bx(B[1]), .Res(C[1]), .Cout(fulladder_2_cout));
  fullAdder fulladder_3 (.Cin(fulladder_2_cout), .Ax(A[2]), .Bx(B[2]), .Res(C[2]), .Cout(fulladder_3_cout));
  fullAdder fulladder_4 (.Cin(fulladder_3_cout), .Ax(A[3]), .Bx(B[3]), .Res(C[3]), .Cout(fulladder_4_cout));
  fullAdder fulladder_5 (.Cin(fulladder_4_cout), .Ax(A[4]), .Bx(B[4]), .Res(C[4]), .Cout(fulladder_5_cout));
  fullAdder fulladder_6 (.Cin(fulladder_5_cout), .Ax(A[5]), .Bx(B[5]), .Res(C[5]), .Cout(fulladder_6_cout));
  fullAdder fulladder_7 (.Cin(fulladder_6_cout), .Ax(A[6]), .Bx(B[6]), .Res(C[6]), .Cout(fulladder_7_cout));
  fullAdder fulladder_8 (.Cin(fulladder_7_cout), .Ax(A[7]), .Bx(B[7]), .Res(C[7]), .Cout(fulladder_8_cout));
  fullAdder fulladder_9 (.Cin(fulladder_8_cout), .Ax(A[8]), .Bx(B[8]), .Res(C[8]), .Cout(fulladder_9_cout));
  fullAdder fulladder_10 (.Cin(fulladder_9_cout), .Ax(A[9]), .Bx(B[9]), .Res(C[9]), .Cout(fulladder_10_cout));
  fullAdder fulladder_11 (.Cin(fulladder_10_cout), .Ax(A[10]), .Bx(B[10]), .Res(C[10]), .Cout(fulladder_11_cout));
  fullAdder fulladder_12 (.Cin(fulladder_11_cout), .Ax(A[11]), .Bx(B[11]), .Res(C[11]), .Cout(fulladder_12_cout));
  fullAdder fulladder_13 (.Cin(fulladder_12_cout), .Ax(A[12]), .Bx(B[12]), .Res(C[12]), .Cout(fulladder_13_cout));
  fullAdder fulladder_14 (.Cin(fulladder_13_cout), .Ax(A[13]), .Bx(B[13]), .Res(C[13]), .Cout(fulladder_14_cout));
  fullAdder fulladder_15 (.Cin(fulladder_14_cout), .Ax(A[14]), .Bx(B[14]), .Res(C[14]), .Cout(fulladder_15_cout));
  fullAdder fulladder_16 (.Cin(fulladder_15_cout), .Ax(A[15]), .Bx(B[15]), .Res(C[15]), .Cout(Cout));
endmodule

module fullAdder (
  input  Cin,
  input  Ax,
  input  Bx,
  output Res,
  output Cout
);

  wire and_1_out, and_2_out, and_3_out, and_4_out, xor_1_out;

  and and_1 (and_1_out, Ax, Cin);
  and and_2 (and_2_out, Ax, Bx);
  or or_1 (Cout, and_1_out, and_2_out, and_3_out);
  and and_3 (and_3_out, Bx, Cin);
  ExactlyOne xor_1 (.out(xor_1_out), .in0(Ax), .in1(Bx), .in2(Cin));
  and and_4 (and_4_out, Ax, Bx, Cin);
  or or_2 (Res, xor_1_out, and_4_out);
endmodule
