// Logisim project nincpu_main.circ as structural Verilog: 1 circuit, main circuit main
module main (
);

  // sixteenRegisterBankEight sixteenregisterbankeight_1: pin names not known
  // ALU alu_1: pin names not known
endmodule
